# Fritzing sketch map (saved by Fritzing 0.9.4)
breadboards: 1

parts:
  Part1 = Arduino Uno (Rev3) - ICSP
  U1 = NodeMCU V1.0
  U2 = 2-Channel 5v Relay Shield [package=relay-2ch5v10a]
  Part2 = MQ-9 breakout
  DHT1 = DHT22 Humidity and Temperature Sensor
  S1 = Pushbutton [package="[SMD]"]
  S2 = Pushbutton [package="[SMD]"]
  LED1 = smd LED [color="Red (633nm)" package="1206 [SMD]"]
  LED2 = smd LED [color="Green (570nm)" package="1206 [SMD]"]
  R1 = Resistor [tolerance=±5% resistance=220 package="0402 [SMD]"]
  R2 = Resistor [tolerance=±5% resistance=220 package="0402 [SMD]"]
  J1 = Piezo Speaker
  PIR1 = PIR sensor
  R3 = Photocell (LDR) [package=THT]
  R4 = Resistor [tolerance=±5% resistance=10k package="0402 [SMD]"]
  R5 = Resistor [tolerance=±5% resistance=10k package="0402 [SMD]"]
  R6 = Resistor [tolerance=±5% resistance=10k package="0402 [SMD]"]
  R7 = Resistor [tolerance=±5% resistance=10k package="0402 [SMD]"]
  R8 = Resistor [tolerance=±5% resistance=1k package="0603 [SMD]"]
  R9 = Resistor [tolerance=±5% resistance=2.2k package="0603 [SMD]"]

nets:
  N1: Part1.A1, Part2.AO
  N2: Part1.A2, R3.pin_0, R4.Pin_0
  N3: Part1.A4/SDA, U1.D2
  N4: Part1.A5/SCL, U1.D0, U1.D1
  GND: Part1.ICSP_MISO, Part1.D12/MISO, Part1.GND, U1.GND, U2.GND, U2.IN1, Part2.GND, DHT1.GND, LED1.cathode, LED2.cathode, J1.pin1, PIR1.GND, R4.Pin_1, R5.Pin_0, R6.Pin_1, R7.Pin_0, R9.Pin_1
  N5: Part1.ICSP_MOSI, Part1.D11_PWM/MOSI, PIR1.SIG
  N6: Part1.D8, DHT1.DATA, R5.Pin_1
  N7: Part1.D9_PWM, R2.Pin_1
  N8: Part1.D10_PWM/SS, J1.pin2
  N9: Part1.D13/SCK, R8.Pin_0
  N10: Part1.D3_PWM, U2.IN2
  N11: Part1.D4, S1.Pin_1, S1.Pin_2, R7.Pin_1
  N12: Part1.D5_PWM, R1.Pin_1
  N13: Part1.D6_PWM, Part2.DO
  N14: Part1.D7, S2.Pin_1, S2.Pin_2, R6.Pin_0
  VCC: Part1.5V, U1.Vin, U2.VCC, Part2.VCC, DHT1.VDD, S1.Pin_3, S1.Pin_4, S2.Pin_3, S2.Pin_4, PIR1.VDD, R3.pin_1
  N15: U1.RST, U1.EN, R8.Pin_1, R9.Pin_0
  N16: LED1.anode, R2.Pin_0
  N17: LED2.anode, R1.Pin_0

custom parts:
  NodeMCU V1.0: ESP8266 based NodeMCU
  2-Channel 5v Relay Shield: 2 Channel 5v Relay Shield w. 2x SPD-06VDC-SD-C
  MQ-9 breakout: SKU: 101284
